// Digital circuit address_decoder.dig as structural Verilog
module address_decoder (
  input  A12,
  input  A13,
  input  A14,
  input  A15,
  input  A8,
  input  A9,
  input  A10,
  output RAMnEN,
  output ROMnEN,
  output LCDnEN__C000_C0FF,
  output VIAnEN__C100_C1FF,
  output SIDnEN__C200_C2FF,
  output nEN__D000_DFFF,
  output EEPROMnEN__C300_C3FF
);

  wire nand_1_out, nand_3_out, nand_5_out, nand_6_out;

  Seven_Seg_Hex seven_seg_hex_1 (.d({A15, A14, A13, A12}), .dp(1'b0));
  nand nand_1 (nand_1_out, A14, A15);
  nand nand_2 (RAMnEN, nand_1_out, nand_1_out);
  nand nand_3 (nand_3_out, A13, A13);
  nand nand_4 (ROMnEN, A13, RAMnEN);
  _74138 _74138_1 (
    .pin1(A8), .pin2(A9), .pin3(A10), .pin4(A13), .pin5(nand_1_out), .pin6(A12), .pin8(1'b0),
    .pin12(EEPROMnEN__C300_C3FF), .pin13(SIDnEN__C200_C2FF), .pin14(VIAnEN__C100_C1FF),
    .pin15(LCDnEN__C000_C0FF), .pin16(1'b1));  // open: pin7, pin9, pin10, pin11
  nand nand_5 (nand_5_out, nand_3_out, A12);
  nand nand_6 (nand_6_out, nand_5_out, nand_5_out);
  nand nand_7 (nEN__D000_DFFF, nand_6_out, RAMnEN);
endmodule
