// Digital circuit address_decoder_v13.dig as structural Verilog
module address_decoder_v13 (
  input  A12,
  input  A13,
  input  A14,
  input  A15,
  input  A8,
  input  A9,
  input  A10,
  output LCDnEN__D000_D0FF,
  output ACIAnEN__D200_D2FF,
  output SIDnEN__D400_D4FF,
  output EEPROMnEN__D300_D3FF,
  output RAMnEN__0000_7FFF,
  output ROMnEN__8000_BFFF__E000_FFFF,
  output VIAnEN__D100_D1FF
);

  wire nand_1_out, nand_2_out, nand_3_out;

  Seven_Seg_Hex seven_seg_hex_1 (.d({A15, A14, A13, A12}), .dp(1'b0));
  nand nand_1 (nand_1_out, A14, A15);
  nand nand_2 (nand_2_out, A13, A14);
  nand nand_3 (nand_3_out, nand_2_out, A14);
  _74138 _74138_1 (
    .pin1(A8), .pin2(A9), .pin3(A10), .pin4(nand_1_out), .pin5(A13), .pin6(A12), .pin8(1'b0),
    .pin11(SIDnEN__D400_D4FF), .pin12(EEPROMnEN__D300_D3FF), .pin13(ACIAnEN__D200_D2FF),
    .pin14(VIAnEN__D100_D1FF), .pin15(LCDnEN__D000_D0FF), .pin16(1'b1));  // open: pin7, pin9, pin10
  nand nand_4 (ROMnEN__8000_BFFF__E000_FFFF, nand_3_out, A15);

  assign RAMnEN__0000_7FFF = A15;
endmodule
