// Digital circuit Fuse.dig as structural Verilog
module Fuse (
  input  [31:0] SQ,
  input  [31:0] F,
  input  Clk,
  input  en,
  output P
);

  wire comparator_1_eq, comparator_2_eq, not_1_out;
  wire [31:0] or_1_out, register_1_q;

  Register #(.Bits(32)) register_1 (.D(F), .C(Clk), .en(en), .Q(register_1_q));
  assign or_1_out = SQ | register_1_q;  // Or or_1, 32 bits wide
  Comparator #(.Bits(32)) comparator_1 (.a(or_1_out), .b({32{1'b1}}), .eq(comparator_1_eq));  // open: gt, lt
  Comparator #(.Bits(32)) comparator_2 (.a(register_1_q), .b({32{1'b1}}), .eq(comparator_2_eq));  // open: gt, lt
  or or_2 (P, not_1_out, comparator_2_eq);
  not not_1 (not_1_out, comparator_1_eq);
endmodule
