// Digital circuit Fuse_matrix.dig as structural Verilog
module Fuse_matrix (
  input  [31:0] SQ,
  input  [31:0] F,
  input  Clk,
  input  [7:0] en,
  output [7:0] P
);

  wire [7:0] fuse_4_p;

  Fuse fuse_1 (.SQ(SQ), .F(F), .Clk(Clk), .en(en[0]), .P(fuse_4_p[0]));
  Fuse fuse_2 (.SQ(SQ), .F(F), .Clk(Clk), .en(en[1]), .P(fuse_4_p[1]));
  Fuse fuse_3 (.SQ(SQ), .F(F), .Clk(Clk), .en(en[2]), .P(fuse_4_p[2]));
  Fuse fuse_4 (.SQ(SQ), .F(F), .Clk(Clk), .en(en[3]), .P(fuse_4_p[3]));
  Fuse fuse_5 (.SQ(SQ), .F(F), .Clk(Clk), .en(en[4]), .P(fuse_4_p[4]));
  Fuse fuse_6 (.SQ(SQ), .F(F), .Clk(Clk), .en(en[5]), .P(fuse_4_p[5]));
  Fuse fuse_7 (.SQ(SQ), .F(F), .Clk(Clk), .en(en[6]), .P(fuse_4_p[6]));
  Fuse fuse_8 (.SQ(SQ), .F(F), .Clk(Clk), .en(en[7]), .P(fuse_4_p[7]));
  assign P = ~fuse_4_p;  // Not not_1, 8 bits wide
endmodule
