// Digital circuit GAL16V8.dig as structural Verilog
module GAL16V8 (
  input  I_0_Clk,
  input  I_1,
  input  I_2,
  input  I_3,
  input  I_4,
  input  I_5,
  input  I_6,
  input  I_7,
  input  I_8,
  input  GND,
  input  I_17_nOE,
  output I_16_Q_7,
  output I_15_Q_6,
  output I_14_Q_5,
  output I_13_Q_4,
  output I_12_Q_3,
  output I_11_Q_2,
  output I_10_Q_1,
  output I_9_Q_0,
  output VCC
);

  wire comparator_1_lt, I_9, I_10, I_11, I_12, I_13, I_14, I_15, I_16, M_en, nOE, olmc_1_noe_o, olmc_1_o,
       olmc_2_noe_o, olmc_2_o, olmc_3_noe_o, olmc_3_o, olmc_4_noe_o, olmc_4_o, olmc_5_noe_o, olmc_5_o,
       olmc_6_noe_o, olmc_6_o, olmc_7_noe_o, olmc_7_o, olmc_8_noe_o, olmc_8_o, Q_0, Q_1, Q_2, Q_3, Q_4, Q_5,
       Q_6, Q_7;
  wire [0:0] M_7;
  wire [1:0] M_5, M_6;
  wire [2:0] M_2, M_3, M_4;
  wire [3:0] M_0, M_1;
  wire [6:0] counter_1_out;
  wire [7:0] decoder_1_out_7, decoder_2_out_7, driver_1_out, driver_2_out, driver_3_out, driver_4_out,
       driver_5_out, driver_6_out, driver_7_out, driver_8_out, fuse_matrix_1_p, fuse_matrix_2_p,
       fuse_matrix_3_p, fuse_matrix_4_p, fuse_matrix_5_p, fuse_matrix_6_p, fuse_matrix_7_p, fuse_matrix_8_p,
       x_en, y_en;
  wire [13:0] register_1_q;
  wire [30:0] SQ;
  wire [31:0] F;

  Comparator #(.Bits(7)) comparator_1 (.a(counter_1_out), .b(7'b1000001), .eq(VCC), .lt(comparator_1_lt));  // open: gt
  Counter #(.Bits(7)) counter_1 (.en(comparator_1_lt), .C(GND), .clr(1'b0), .out(counter_1_out));  // open: ovf
  ROM #(.AddrBits(7), .Bits(32)) Fuses (.A(counter_1_out), .sel(1'b1), .D(F));
  Decoder #(.Selector_Bits(3)) decoder_1 (
    .sel(counter_1_out[2:0]), .out_0(decoder_1_out_7[0]), .out_1(decoder_1_out_7[1]),
    .out_2(decoder_1_out_7[2]), .out_3(decoder_1_out_7[3]), .out_4(decoder_1_out_7[4]),
    .out_5(decoder_1_out_7[5]), .out_6(decoder_1_out_7[6]), .out_7(decoder_1_out_7[7]));
  Decoder #(.Selector_Bits(3)) decoder_2 (
    .sel(counter_1_out[5:3]), .out_0(decoder_2_out_7[0]), .out_1(decoder_2_out_7[1]),
    .out_2(decoder_2_out_7[2]), .out_3(decoder_2_out_7[3]), .out_4(decoder_2_out_7[4]),
    .out_5(decoder_2_out_7[5]), .out_6(decoder_2_out_7[6]), .out_7(decoder_2_out_7[7]));
  assign x_en = ~counter_1_out[6] ? decoder_1_out_7 : 8'bz;  // DriverInvSel driverinvsel_1
  and and_1 (M_en, decoder_1_out_7[0], decoder_2_out_7[0], counter_1_out[6]);
  assign y_en = ~counter_1_out[6] ? decoder_2_out_7 : 8'bz;  // DriverInvSel driverinvsel_2
  PullDown #(.Bits(8)) pulldown_1 (.out(x_en));
  PullDown #(.Bits(8)) pulldown_2 (.out(y_en));
  Register #(.Bits(32)) register_1 (
    .D(F), .C(GND), .en(M_en),
    .Q({M_0[0], M_1[0], M_2[0], M_3[0], M_4[0], M_5[0], M_6[0], M_7[0], M_0[2], M_1[2], M_2[2], M_3[2], M_4[2:1], M_5[1], M_6[1], M_0[1], M_1[3], register_1_q}));
  assign driver_1_out = y_en[0] ? x_en : 8'bz;  // Driver driver_1
  assign driver_2_out = y_en[1] ? x_en : 8'bz;  // Driver driver_2
  assign driver_3_out = y_en[2] ? x_en : 8'bz;  // Driver driver_3
  assign driver_4_out = y_en[3] ? x_en : 8'bz;  // Driver driver_4
  assign driver_5_out = y_en[4] ? x_en : 8'bz;  // Driver driver_5
  assign driver_6_out = y_en[5] ? x_en : 8'bz;  // Driver driver_6
  assign driver_7_out = y_en[6] ? x_en : 8'bz;  // Driver driver_7
  assign driver_8_out = y_en[7] ? x_en : 8'bz;  // Driver driver_8
  Fuse_matrix fuse_matrix_1 (
    .SQ({I_1, SQ[30], Q_0, SQ[28], I_2, SQ[26], Q_1, SQ[24], I_3, SQ[22], Q_2, SQ[20], I_4, SQ[18], Q_3, SQ[16], I_5, SQ[14], Q_4, SQ[12], I_6, SQ[10], Q_5, SQ[8], I_7, SQ[6], Q_6, SQ[4], I_8, SQ[2], Q_7, SQ[0]}),
    .F(F), .Clk(GND), .en(driver_1_out), .P(fuse_matrix_1_p));
  PullDown #(.Bits(8)) pulldown_3 (.out(driver_1_out));
  Fuse_matrix fuse_matrix_2 (
    .SQ({I_1, SQ[30], Q_0, SQ[28], I_2, SQ[26], Q_1, SQ[24], I_3, SQ[22], Q_2, SQ[20], I_4, SQ[18], Q_3, SQ[16], I_5, SQ[14], Q_4, SQ[12], I_6, SQ[10], Q_5, SQ[8], I_7, SQ[6], Q_6, SQ[4], I_8, SQ[2], Q_7, SQ[0]}),
    .F(F), .Clk(GND), .en(driver_2_out), .P(fuse_matrix_2_p));
  PullDown #(.Bits(8)) pulldown_4 (.out(driver_2_out));
  Fuse_matrix fuse_matrix_3 (
    .SQ({I_1, SQ[30], Q_0, SQ[28], I_2, SQ[26], Q_1, SQ[24], I_3, SQ[22], Q_2, SQ[20], I_4, SQ[18], Q_3, SQ[16], I_5, SQ[14], Q_4, SQ[12], I_6, SQ[10], Q_5, SQ[8], I_7, SQ[6], Q_6, SQ[4], I_8, SQ[2], Q_7, SQ[0]}),
    .F(F), .Clk(GND), .en(driver_3_out), .P(fuse_matrix_3_p));
  PullDown #(.Bits(8)) pulldown_5 (.out(driver_3_out));
  Fuse_matrix fuse_matrix_4 (
    .SQ({I_1, SQ[30], Q_0, SQ[28], I_2, SQ[26], Q_1, SQ[24], I_3, SQ[22], Q_2, SQ[20], I_4, SQ[18], Q_3, SQ[16], I_5, SQ[14], Q_4, SQ[12], I_6, SQ[10], Q_5, SQ[8], I_7, SQ[6], Q_6, SQ[4], I_8, SQ[2], Q_7, SQ[0]}),
    .F(F), .Clk(GND), .en(driver_4_out), .P(fuse_matrix_4_p));
  PullDown #(.Bits(8)) pulldown_6 (.out(driver_4_out));
  Fuse_matrix fuse_matrix_5 (
    .SQ({I_1, SQ[30], Q_0, SQ[28], I_2, SQ[26], Q_1, SQ[24], I_3, SQ[22], Q_2, SQ[20], I_4, SQ[18], Q_3, SQ[16], I_5, SQ[14], Q_4, SQ[12], I_6, SQ[10], Q_5, SQ[8], I_7, SQ[6], Q_6, SQ[4], I_8, SQ[2], Q_7, SQ[0]}),
    .F(F), .Clk(GND), .en(driver_5_out), .P(fuse_matrix_5_p));
  PullDown #(.Bits(8)) pulldown_7 (.out(driver_5_out));
  Fuse_matrix fuse_matrix_6 (
    .SQ({I_1, SQ[30], Q_0, SQ[28], I_2, SQ[26], Q_1, SQ[24], I_3, SQ[22], Q_2, SQ[20], I_4, SQ[18], Q_3, SQ[16], I_5, SQ[14], Q_4, SQ[12], I_6, SQ[10], Q_5, SQ[8], I_7, SQ[6], Q_6, SQ[4], I_8, SQ[2], Q_7, SQ[0]}),
    .F(F), .Clk(GND), .en(driver_6_out), .P(fuse_matrix_6_p));
  PullDown #(.Bits(8)) pulldown_8 (.out(driver_6_out));
  Fuse_matrix fuse_matrix_7 (
    .SQ({I_1, SQ[30], Q_0, SQ[28], I_2, SQ[26], Q_1, SQ[24], I_3, SQ[22], Q_2, SQ[20], I_4, SQ[18], Q_3, SQ[16], I_5, SQ[14], Q_4, SQ[12], I_6, SQ[10], Q_5, SQ[8], I_7, SQ[6], Q_6, SQ[4], I_8, SQ[2], Q_7, SQ[0]}),
    .F(F), .Clk(GND), .en(driver_7_out), .P(fuse_matrix_7_p));
  PullDown #(.Bits(8)) pulldown_9 (.out(driver_7_out));
  Fuse_matrix fuse_matrix_8 (
    .SQ({I_1, SQ[30], Q_0, SQ[28], I_2, SQ[26], Q_1, SQ[24], I_3, SQ[22], Q_2, SQ[20], I_4, SQ[18], Q_3, SQ[16], I_5, SQ[14], Q_4, SQ[12], I_6, SQ[10], Q_5, SQ[8], I_7, SQ[6], Q_6, SQ[4], I_8, SQ[2], Q_7, SQ[0]}),
    .F(F), .Clk(GND), .en(driver_8_out), .P(fuse_matrix_8_p));
  PullDown #(.Bits(8)) pulldown_10 (.out(driver_8_out));
  not not_1 (M_0[3], M_0[1]);
  // Probe on fuse_matrix_1_p
  // Probe on fuse_matrix_2_p
  // Probe on fuse_matrix_3_p
  // Probe on fuse_matrix_4_p
  // Probe on fuse_matrix_5_p
  // Probe on fuse_matrix_6_p
  // Probe on fuse_matrix_7_p
  // Probe on fuse_matrix_8_p
  OLMC olmc_1 (
    .P(fuse_matrix_1_p), .I(I_9), .C(I_0_Clk), .Clk(I_0_Clk), .nOE_i(nOE), .M(M_0), .nOE_o(olmc_1_noe_o),
    .O(olmc_1_o), .Q(Q_0));
  OLMC olmc_2 (
    .P(fuse_matrix_2_p), .I(I_10), .C(I_9), .Clk(I_0_Clk), .nOE_i(nOE), .M({M_1[3:2], M_0[2], M_1[0]}),
    .nOE_o(olmc_2_noe_o), .O(olmc_2_o), .Q(Q_1));
  OLMC olmc_3 (
    .P(fuse_matrix_3_p), .I(I_11), .C(I_10), .Clk(I_0_Clk), .nOE_i(nOE),
    .M({M_1[3], M_2[2], M_1[2], M_2[0]}), .nOE_o(olmc_3_noe_o), .O(olmc_3_o), .Q(Q_2));
  OLMC olmc_4 (
    .P(fuse_matrix_4_p), .I(I_12), .C(I_11), .Clk(I_0_Clk), .nOE_i(nOE),
    .M({M_1[3], M_3[2], M_2[2], M_3[0]}), .nOE_o(olmc_4_noe_o), .O(olmc_4_o), .Q(Q_3));
  OLMC olmc_5 (
    .P(fuse_matrix_5_p), .I(I_13), .C(I_14), .Clk(I_0_Clk), .nOE_i(nOE), .M({M_1[3], M_4}),
    .nOE_o(olmc_5_noe_o), .O(olmc_5_o), .Q(Q_4));
  OLMC olmc_6 (
    .P(fuse_matrix_6_p), .I(I_14), .C(I_15), .Clk(I_0_Clk), .nOE_i(nOE), .M({M_1[3], M_4[1], M_5}),
    .nOE_o(olmc_6_noe_o), .O(olmc_6_o), .Q(Q_5));
  OLMC olmc_7 (
    .P(fuse_matrix_7_p), .I(I_15), .C(I_16), .Clk(I_0_Clk), .nOE_i(nOE), .M({M_1[3], M_5[1], M_6}),
    .nOE_o(olmc_7_noe_o), .O(olmc_7_o), .Q(Q_6));
  OLMC olmc_8 (
    .P(fuse_matrix_8_p), .I(I_16), .C(I_17_nOE), .Clk(I_0_Clk), .nOE_i(nOE),
    .M({M_0[3], M_6[1], M_0[1], M_7[0]}), .nOE_o(olmc_8_noe_o), .O(olmc_8_o), .Q(Q_7));
  // PinControl pincontrol_1: pin names not known; wires that end beside it: olmc_1_o, olmc_1_noe_o, olmc_2_noe_o, I_9, I_9_Q_0
  // PinControl pincontrol_2: pin names not known; wires that end beside it: olmc_2_o, olmc_3_noe_o, I_10, I_10_Q_1
  // PinControl pincontrol_3: pin names not known; wires that end beside it: olmc_3_o, olmc_4_noe_o, I_11, I_11_Q_2
  // PinControl pincontrol_4: pin names not known; wires that end beside it: olmc_4_o, olmc_5_noe_o, I_12, I_12_Q_3
  // PinControl pincontrol_5: pin names not known; wires that end beside it: olmc_5_o, olmc_6_noe_o, I_13, I_13_Q_4
  // PinControl pincontrol_6: pin names not known; wires that end beside it: olmc_6_o, olmc_7_noe_o, I_14, I_14_Q_5
  // PinControl pincontrol_7: pin names not known; wires that end beside it: olmc_7_o, olmc_8_noe_o, I_15, I_15_Q_6
  // PinControl pincontrol_8: pin names not known; wires that end beside it: olmc_8_o, I_16, I_16_Q_7
  not not_2 (nOE, I_17_nOE);
  not not_3 (SQ[0], Q_7);
  not not_4 (SQ[2], I_8);
  not not_5 (SQ[4], Q_6);
  not not_6 (SQ[6], I_7);
  not not_7 (SQ[8], Q_5);
  not not_8 (SQ[10], I_6);
  not not_9 (SQ[12], Q_4);
  not not_10 (SQ[14], I_5);
  not not_11 (SQ[16], Q_3);
  not not_12 (SQ[18], I_4);
  not not_13 (SQ[20], Q_2);
  not not_14 (SQ[22], I_3);
  not not_15 (SQ[24], Q_1);
  not not_16 (SQ[26], I_2);
  not not_17 (SQ[28], Q_0);
  not not_18 (SQ[30], I_1);

  // Other names for the same wires on the sheet: M_2 (some bits) = M_1[3:2]; M_3 (some bits) = {M_1[3], M_2[2]};
  //   M_4[3] = M_1[3]; M_5[3:2] = {M_1[3], M_4[1]}; M_6[3:2] = {M_1[3], M_5[1]}; M_7[3:1] = {M_0[3], M_6[1], M_0[1]};
  //   M_1[1] = M_0[2]; C = GND; Clk = I_0_Clk; I_0 = I_0_Clk;
  //   SQ (some bits) = {I_1, Q_0, I_2, Q_1, I_3, Q_2, I_4, Q_3, I_5, Q_4, I_6, Q_5, I_7, Q_6, I_8, Q_7};
  //   I_17 = I_17_nOE

  // Notes on the sheet:
  //   GND: Hz: 50
  //   contents of Fuses (hex, n*v repeats v):
  //   7fff7bff,efffbbff,ffffffff,ffffffff,ffffffff,ffffffff,ffffffff,ffffffff,f7ff7bff,
  //   deffbbff,edffbbff,ffffffff,ffffffff,ffffffff,ffffffff,ffffffff,ff7f7bff,fedfbbff,
  //   efdfbbff,ddefbbff,ffffffff,ffffffff,ffffffff,ffffffff,fff77bff,ffedbbff,fefdbbff,
  //   effdbbff,dddebbff,ffffffff,ffffffff,ffffffff,ffffffff,ffffffff,ffffffff,ffffffff,
  //   ffffffff,ffffffff,ffffffff,ffffffff,ffffffff,ffffffff,ffffffff,ffffffff,ffffffff,
  //   ffffffff,ffffffff,ffffffff,ffffffff,ffffffff,ffffffff,ffffffff,ffffffff,ffffffff,
  //   ffffffff,ffffffff,ffffffff,ffffffff,ffffffff,ffffffff,ffffffff,ffffffff,ffffffff,
  //   ffffffff,f0007fff
endmodule
