// Digital circuit OLMC.dig as structural Verilog
module OLMC (
  input  [7:0] P,
  input  I,
  input  C,
  input  Clk,
  input  nOE_i,
  input  [3:0] M,
  output nOE_o,
  output O,
  output Q
);

  wire d_ff_1_nq, d_ff_1_q, multiplexer_1_out, multiplexer_5_out, nand_1_out, nor_1_out, or_1_out, xor_1_out;
  wire [1:1] multiplexer_3_out;

  Multiplexer multiplexer_1 (.sel(nand_1_out), .in_0(1'b0), .in_1(P[0]), .out(multiplexer_1_out));
  or or_1 (or_1_out, multiplexer_1_out, P[1], P[2], P[3], P[4], P[5], P[6], P[7]);
  Multiplexer #(.Selector_Bits(2)) multiplexer_2 (
    .sel(M[3:2]), .in_0(1'b1), .in_1(1'b0), .in_2(nOE_i), .in_3(P[0]), .out(nOE_o));
  nand nand_1 (nand_1_out, M[2], M[3]);
  xor xor_1 (xor_1_out, or_1_out, M[0]);
  Multiplexer multiplexer_3 (.sel(M[3]), .in_0(M[1]), .in_1(M[2]), .out(multiplexer_3_out[1]));
  Multiplexer #(.Selector_Bits(2)) multiplexer_4 (
    .sel({multiplexer_3_out[1], M[3]}), .in_0(1'b0), .in_1(d_ff_1_nq), .in_2(C), .in_3(I), .out(Q));
  nor nor_1 (nor_1_out, ~M[3], M[2]);  // NOr
  D_FF d_ff_1 (.D(xor_1_out), .C(Clk), .Q(d_ff_1_q), .nQ(d_ff_1_nq));
  Multiplexer multiplexer_5 (.sel(nor_1_out), .in_0(xor_1_out), .in_1(d_ff_1_q), .out(multiplexer_5_out));
  not not_1 (O, multiplexer_5_out);

  // Other names for the same wires on the sheet: XOr = M[0]; AC_m_1 = M[1]; AC_n_1 = M[2]; AC_0 = M[3]; nOE = nOE_i
endmodule
