// Digital circuit addr_test.dig as structural Verilog
module addr_test (
  input  A_8,
  input  clk,
  input  nOE,
  input  A_9,
  input  A_10,
  input  A_12,
  input  A_13,
  input  A_14,
  input  A_15
);

  wire Clk_out, undriven, undriven_2, undriven_3, undriven_4, undriven_5, undriven_6, undriven_7, undriven_8,
       undriven_9;

  Button u_Clk (.out(Clk_out));
  GAL16V8 gal16v8_1 ();
  LED led_1 (.in(undriven));
  LED nIO5 (.in(undriven_2));
  LED nIO4 (.in(undriven_3));
  LED nIO3 (.in(undriven_4));
  LED nIO2 (.in(undriven_5));
  LED nVIA (.in(undriven_6));
  LED nLCD (.in(undriven_7));
  LED nROM (.in(undriven_8));
  LED nRAM (.in(undriven_9));

  // Notes on the sheet:
  //   clk: Hz: 50
  //   contents of Fuses (hex, n*v repeats v):
  //   ../../gal/src/addr.hex false
endmodule
