// Digital circuit slowbus_test.dig as structural Verilog
module slowbus_test (
  input  nSLOW,
  input  nOE,
  input  RnW,
  input  in_4,
  input  in_5,
  input  in_6,
  input  in_7,
  input  in_8,
  input  clk
);

  wire CLK_out, undriven, undriven_2, undriven_3, undriven_4, undriven_5, undriven_6, undriven_7, undriven_8;

  Button u_CLK (.out(CLK_out));
  GAL16V8 gal16v8_1 ();
  LED led_1 (.in(undriven));
  LED nWD (.in(undriven_2));
  LED nRD (.in(undriven_3));
  LED Q0 (.in(undriven_4));
  LED Q1 (.in(undriven_5));
  LED Q2 (.in(undriven_6));
  LED PHI2 (.in(undriven_7));
  LED PHV (.in(undriven_8));

  // Notes on the sheet:
  //   nSLOW: default 1
  //   RnW: default 1
  //   clk: Hz: 300
  //   =CLK/2
  //   =CLK/2 if /SLOW = 1
  //   =CLK/8 if /SLOW = 0
  //   contents of Fuses (hex, n*v repeats v):
  //   /home/anderson/src/m6502/gal/src/slowbus16.hex false
endmodule
