// Digital circuit stretch_161.dig as structural Verilog
module stretch_161 (
  input  clk,
  input  nSLOW,
  input  nRESET,
  output CLK_HI,
  output CLK_LO
);

  wire _74161_1_p1;

  // _74161 _74161_1: pin names not known; wires that end beside it: _74161_1_p1, nRESET, clk, 1'b1, 1'b1, 1'b1, nSLOW, nSLOW, 1'b1, 1'b1, 1'b0, CLK_HI, CLK_LO, _74161_1_p1

  // Notes on the sheet:
  //   nSLOW: default 1
  //   nRESET: default 1
endmodule
