// Digital circuit ram_banking_2.dig as structural Verilog
module ram_banking_2 (
  input  \Ф2 ,
  input  in_3,
  input  in_4,
  input  in_5,
  input  in_6,
  input  in_7,
  input  in_8,
  input  in_9,
  input  in_10,
  input  nEN,
  input  nACCESS,
  input  A12,
  input  A13,
  input  A14,
  input  A12_2,
  input  A13_2,
  input  A14_2,
  output A15,
  output A16,
  output A17,
  output A18,
  output nACCESS_2,
  output nACCESS_3
);

  wire nand_1_out, nand_2_out, nand_3_out, nor_1_out, nor_2_out, not_1_out, not_2_out, not_3_out, not_4_out,
       not_5_out;

  not not_1 (not_1_out, A12);
  not not_2 (not_2_out, A13);
  not not_3 (not_3_out, A14);
  not not_4 (not_4_out, nEN);
  nand nand_1 (nand_1_out, not_1_out, not_2_out);
  nor nor_1 (nor_1_out, A12_2, A13_2);
  nand nand_2 (nand_2_out, \Ф2 , not_4_out);
  nor nor_2 (nor_2_out, nor_1_out, nor_1_out);
  not not_5 (not_5_out, nand_1_out);
  nand nand_3 (nand_3_out, not_5_out, not_3_out);
  nor nor_3 (nACCESS_3, nor_2_out, A14_2);
  // _74574 _74574_1: pin names not known; wires that end beside it: nACCESS, nand_2_out, in_3, in_4, in_5, in_6, in_7, in_8, in_9, in_10, 1'b1, 1'b0, A15, A16, A17, A18
  not not_6 (nACCESS_2, nand_3_out);
  PullUp pullup_1 (.out(A15));
  PullUp pullup_2 (.out(A16));
  PullUp pullup_3 (.out(A17));
  PullUp pullup_4 (.out(A18));

  // Notes on the sheet:
  //   nEN: default 1
  //   nACCESS: default 1
  //   Bank register select
  //   Asserted for 0x1000..0x7FFF (low if A14 | A13 | A12 == 1)
  //   To RAM
endmodule
