// Digital circuit ram_banking_3.dig as structural Verilog
module ram_banking_3 (
  input  D0,
  input  D1,
  input  D2,
  input  D3,
  input  A0,
  input  A1,
  input  A13,
  input  A14,
  input  BANKnWR,
  input  in_14,
  input  in_15,
  input  in_16,
  input  in_17,
  input  in_18,
  input  in_19,
  input  in_20,
  input  in_21,
  input  in_22,
  input  in_23,
  output A15,
  output A16,
  output A17,
  output A18,
  output A19,
  output A20,
  output A21,
  output A22
);

  // _74157 _74157_1: pin names not known; wires that end beside it: in_23, in_22, in_21, in_20, in_18, in_19, in_17, in_16, in_15, in_14, 1'b1, 1'b0, A19, A20, A21, A22
  // _74670 _74670_1: pin names not known; wires that end beside it: D0, D1, D2, D3, A0, A1, A13, A14, 1'b0, BANKnWR, 1'b1, 1'b0, A15, A16, A17, A18

  // Notes on the sheet:
  //   BANKnWR: default 1
  //   in_14: default 1
  //   in_15: default 1
  //   in_16: default 1
  //   in_17: default 1
  //   in_18: default 1
  //   in_19: default 1
  //   in_20: default 1
  //   in_21: default 1
  //   in_22: default 1
  //   in_23: default 1
  //   Set bank
  //   Bank select
  //   Use bank
endmodule
