// Digital circuit ram_banking_4.dig as structural Verilog
module ram_banking_4 (
  input  D0,
  input  D1,
  input  D2,
  input  D3,
  input  A0,
  input  A1,
  input  A13,
  input  A14,
  input  BANKnEN,
  input  nRD,
  input  nWD,
  output A15,
  output A16,
  output A17,
  output A18,
  output D0_2,
  output D1_2,
  output D2_2,
  output D3_2
);

  wire _74157_1_p4, _74157_1_p5, _74157_1_p8, _74157_1_p9, _74157_1_p13, _74157_1_p14, _74244_1_p6,
       _74244_1_p7, _74244_1_p8, _74244_1_p9, _74244_1_p10, nand_1_out, nand_2_out, not_1_out, not_2_out,
       not_3_out;

  not not_1 (not_1_out, nWD);
  not not_2 (not_2_out, nRD);
  not not_3 (not_3_out, BANKnEN);
  nand nand_1 (nand_1_out, not_3_out, not_1_out);
  nand nand_2 (nand_2_out, not_3_out, not_2_out);
  // _74157 _74157_1: pin names not known; wires that end beside it: BANKnEN, A0, A1, _74157_1_p4, _74157_1_p5, A13, A14, _74157_1_p8, _74157_1_p9, 1'b0, 1'b1, 1'b0, _74157_1_p13, _74157_1_p14
  // NotConnected on _74157_1_p4
  // NotConnected on _74157_1_p5
  // NotConnected on _74157_1_p8
  // NotConnected on _74157_1_p9
  // _74670 _74670_1: pin names not known; wires that end beside it: D0, D1, D2, D3, A0, A1, _74157_1_p13, _74157_1_p14, 1'b0, nand_1_out, 1'b1, 1'b0, A15, A16, A17, A18
  // _74244 _74244_1: pin names not known; wires that end beside it: A15, A16, A17, A18, nand_2_out, _74244_1_p6, _74244_1_p7, _74244_1_p8, _74244_1_p9, _74244_1_p10, 1'b1, 1'b0, D0_2, D1_2, D2_2, D3_2
  // NotConnected on _74244_1_p6
  // NotConnected on _74244_1_p7
  // NotConnected on _74244_1_p8
  // NotConnected on _74244_1_p9
  // NotConnected on _74244_1_p10

  // Notes on the sheet:
  //   BANKnEN: default 1
  //   nRD: default 1
  //   nWD: default 1
endmodule
