// Digital circuit read_write_selector.dig as structural Verilog
module read_write_selector (
  input  R_W,
  input  \Ф2 ,
  output out_3,
  output out_4
);

  wire nand_1_out, not_1_out, not_2_out;

  nand nand_1 (nand_1_out, R_W, R_W);
  nand nand_2 (out_3, nand_1_out, \Ф2 );
  nand nand_3 (out_4, \Ф2 , R_W);
  not not_1 (not_1_out, out_3);
  not not_2 (not_2_out, out_4);
  LED WD (.in(not_1_out));
  LED RD (.in(not_2_out));

  // Notes on the sheet:
  //   Ф2: Hz: 2
endmodule
