// Digital circuit rom_banking.dig as structural Verilog
module rom_banking (
  input  D0,
  input  nRES,
  input  nEN,
  input  D1,
  input  D2,
  input  D3,
  input  D4,
  input  D5,
  input  D6,
  input  D7,
  input  \Ф1 ,
  input  in_17,
  output A13,
  output A14,
  output A15,
  output _1st,
  output _2nd
);

  wire nand_1_out, not_1_out;

  not not_1 (not_1_out, nEN);
  not not_2 (_2nd, \Ф1 );
  nand nand_1 (nand_1_out, \Ф1 , not_1_out);
  // NAnd nand_2 has open pins: In_1=nand_1_out, In_2=nand_1_out, out=open
  // _74273 _74273_1: pin names not known; wires that end beside it: in_17, nRES, D0, D1, D2, D3, D4, D5, D6, D7, 1'b1, 1'b0, A13, A14, A15

  assign _1st = \Ф1 ;

  // Notes on the sheet:
  //   nRES: default 1
  //   nEN: default 1
  //   in_17: default 1
  //   (~{Ф2})
  //   (To address decoder)
  //   (To ROM)
endmodule
