// Digital circuit rom_banking_2.dig as structural Verilog
module rom_banking_2 (
  input  \Ф2 ,
  input  in_3,
  input  in_4,
  input  in_5,
  input  in_6,
  input  in_7,
  input  in_8,
  input  in_9,
  input  in_10,
  input  nEN,
  input  nACCESS,
  output out_1,
  output out_12,
  output out_13,
  output out_14,
  output out_15,
  output out_16,
  output out_17,
  output out_18
);

  wire nand_1_out, not_1_out;

  not not_1 (not_1_out, nEN);
  nand nand_1 (nand_1_out, \Ф2 , not_1_out);
  // _74573 _74573_1: pin names not known; wires that end beside it: nACCESS, nand_1_out, in_3, in_4, in_5, in_6, in_7, in_8, in_9, in_10, 1'b1, 1'b0, out_1, out_12, out_13, out_14, out_15, out_16, out_17, out_18

  // Notes on the sheet:
  //   nEN: default 1
  //   nACCESS: default 1
  //   Bank register select
  //   Asserted for 0x1000..0x7FFF (A14 | A13 | A12 == 1)
endmodule
