// Digital circuit rw_banking.dig as structural Verilog
module rw_banking (
  input  D3,
  input  D2,
  input  D1,
  input  D0,
  input  nRES,
  input  BANKnEN,
  input  RnW,
  output A18,
  output A17,
  output A16,
  output A15,
  output D0_2,
  output D1_2,
  output D2_2,
  output D3_2
);

  wire _74244_1_p1, _74244_1_p2, _74244_1_p3, _74244_1_p4, _74244_1_p5, _74273_1_p7, _74273_1_p8,
       _74273_1_p9, _74273_1_p10, nand_1_out, nand_2_out, nand_3_out, nand_4_out;

  nand nand_1 (nand_1_out, BANKnEN, BANKnEN);
  nand nand_2 (nand_2_out, RnW, RnW);
  nand nand_3 (nand_3_out, nand_1_out, nand_2_out);
  nand nand_4 (nand_4_out, nand_1_out, RnW);
  // _74273 _74273_1: pin names not known; wires that end beside it: nand_3_out, nRES, D3, D2, D1, D0, _74273_1_p7, _74273_1_p8, _74273_1_p9, _74273_1_p10, 1'b1, 1'b0, A18, A17, A16, A15
  // NotConnected on _74273_1_p7
  // NotConnected on _74273_1_p8
  // NotConnected on _74273_1_p9
  // NotConnected on _74273_1_p10
  // _74244 _74244_1: pin names not known; wires that end beside it: _74244_1_p1, _74244_1_p2, _74244_1_p3, _74244_1_p4, _74244_1_p5, A18, A17, A16, A15, nand_4_out, 1'b1, 1'b0, D3_2, D2_2, D1_2, D0_2
  // NotConnected on _74244_1_p1
  // NotConnected on _74244_1_p2
  // NotConnected on _74244_1_p3
  // NotConnected on _74244_1_p4
  // NotConnected on _74244_1_p5

  // Notes on the sheet:
  //   nRES: default 1
  //   BANKnEN: default 1
  //   RnW: default 1
  //   Data in
  //   Data out
  //   BANK~EN=0
  //   R~W=0
  //   BANK~EN=0
  //   R~W=1
  //   To RAM
endmodule
