// Digital circuit sevenseg_decoder.dig as structural Verilog
module sevenseg_decoder (
  input  D7,
  input  \Ф2 ,
  input  D6,
  input  D5,
  input  D4,
  input  D3,
  input  D2,
  input  D1,
  input  D0
);

  wire _74157_1_pin1, _74157_1_pin4, _74157_1_pin7, _74157_1_pin9, _74157_1_pin12, and_1_out, and_2_out,
       and_3_out, and_4_out, and_5_out, and_6_out, and_7_out, and_8_out, and_9_out, and_10_out, and_11_out,
       and_12_out, and_13_out, and_14_out, and_15_out, and_16_out, and_17_out, and_18_out, and_19_out,
       and_20_out, and_21_out, and_22_out, and_23_out, and_24_out, and_25_out, and_26_out, and_27_out,
       and_28_out, and_29_out, and_30_out, fgnfet_1_d, fgnfet_2_d, jk_ff_as_1_nq, not_1_out, not_2_out,
       not_3_out, not_4_out, or_1_out, or_2_out, or_3_out, or_4_out, or_5_out, or_6_out, or_7_out;

  not not_1 (not_1_out, _74157_1_pin4);
  _74157 _74157_1 (
    .pin1(_74157_1_pin1), .pin2(D7), .pin3(D3), .pin4(_74157_1_pin4), .pin5(D6), .pin6(D2),
    .pin7(_74157_1_pin7), .pin8(1'b0), .pin9(_74157_1_pin9), .pin10(D1), .pin11(D5), .pin12(_74157_1_pin12),
    .pin13(D0), .pin14(D4), .pin15(1'b0), .pin16(1'b1));
  not not_2 (not_2_out, _74157_1_pin7);
  not not_3 (not_3_out, _74157_1_pin9);
  not not_4 (not_4_out, _74157_1_pin12);
  and and_1 (and_1_out, not_1_out, _74157_1_pin7, _74157_1_pin12);
  and and_2 (and_2_out, not_3_out, _74157_1_pin12);
  and and_3 (and_3_out, _74157_1_pin4, not_2_out);
  and and_4 (and_4_out, not_2_out, _74157_1_pin9);
  and and_5 (and_5_out, not_1_out, _74157_1_pin9);
  and and_6 (and_6_out, _74157_1_pin7, _74157_1_pin9, not_4_out);
  and and_7 (and_7_out, _74157_1_pin4, not_4_out);
  and and_8 (and_8_out, _74157_1_pin4, _74157_1_pin7);
  and and_9 (and_9_out, _74157_1_pin4, not_3_out);
  and and_10 (and_10_out, _74157_1_pin4, _74157_1_pin12);
  and and_11 (and_11_out, _74157_1_pin4, not_2_out, not_3_out);
  and and_12 (and_12_out, not_1_out, not_3_out);
  and and_13 (and_13_out, not_2_out, not_4_out);
  and and_14 (and_14_out, _74157_1_pin4, _74157_1_pin9);
  and and_15 (and_15_out, not_2_out, not_3_out);
  and and_16 (and_16_out, _74157_1_pin4, not_3_out, _74157_1_pin12);
  and and_17 (and_17_out, not_1_out, _74157_1_pin7, not_3_out);
  and and_18 (and_18_out, not_1_out, _74157_1_pin9, _74157_1_pin12);
  and and_19 (and_19_out, _74157_1_pin7, _74157_1_pin9);
  and and_20 (and_20_out, not_2_out, _74157_1_pin9, _74157_1_pin12);
  and and_21 (and_21_out, not_1_out, not_3_out, not_4_out);
  and and_22 (and_22_out, not_1_out, _74157_1_pin12);
  and and_23 (and_23_out, not_3_out, not_4_out);
  and and_24 (and_24_out, _74157_1_pin7, not_4_out);
  and and_25 (and_25_out, not_1_out, _74157_1_pin7);
  and and_26 (and_26_out, _74157_1_pin9, not_4_out);
  and and_27 (and_27_out, not_1_out, not_2_out, not_4_out);
  and and_28 (and_28_out, _74157_1_pin7, not_3_out, _74157_1_pin12);
  or or_1 (or_1_out, and_11_out, and_1_out, and_7_out, and_5_out, and_19_out, and_13_out);
  JK_FF_AS jk_ff_as_1 (.Set(1'b0), .J(1'b1), .C(\Ф2 ), .K(1'b1), .Clr(1'b0), .Q(_74157_1_pin1), .nQ(jk_ff_as_1_nq));
  or or_2 (or_2_out, and_21_out, and_18_out, and_16_out, and_15_out, and_13_out);
  and and_29 (and_29_out, _74157_1_pin1, \Ф2 );
  and and_30 (and_30_out, \Ф2 , jk_ff_as_1_nq);
  or or_3 (or_3_out, and_12_out, and_22_out, and_2_out, and_25_out, and_3_out);
  FGNFET fgnfet_1 (.G(and_29_out), .D(fgnfet_1_d), .S(1'b0));
  FGNFET fgnfet_2 (.G(and_30_out), .D(fgnfet_2_d), .S(1'b0));
  Seven_Seg #(.commonCathode("true")) seven_seg_1 (
    .a(or_1_out), .b(or_2_out), .c(or_3_out), .d(or_4_out), .e(or_5_out), .f(or_6_out), .g(or_7_out),
    .dp(1'b0), .common(fgnfet_2_d));
  or or_4 (or_4_out, and_27_out, and_20_out, and_28_out, and_6_out, and_9_out);
  or or_5 (or_5_out, and_13_out, and_26_out, and_14_out, and_8_out);
  Seven_Seg #(.commonCathode("true")) seven_seg_2 (
    .a(or_1_out), .b(or_2_out), .c(or_3_out), .d(or_4_out), .e(or_5_out), .f(or_6_out), .g(or_7_out),
    .dp(1'b0), .common(fgnfet_1_d));
  or or_6 (or_6_out, and_17_out, and_23_out, and_24_out, and_3_out, and_14_out);
  or or_7 (or_7_out, and_17_out, and_4_out, and_26_out, and_3_out, and_10_out);

  // Notes on the sheet:
  //   /ABD
  //   /CD
  //   A/B
  //   /BC
  //   /AC
  //   BC/D
  //   A/D
  //   AB
  //   A/C
  //   AD
  //   A/B/C
  //   /A/C
  //   /B/D
  //   AC
  //   /B/C
  //   A/CD
  //   /AB/C
  //   /ACD
  //   BC
  //   /BCD
  //   /A/C/D
  //   /AD
  //   /C/D
  //   B/D
  //   /AB
  //   C/D
  //   /A/B/D
  //   B/CD
endmodule
