// Digital circuit spi.dig as structural Verilog
module spi (
  input  MISO,
  input  DRIVE,
  input  nRD,
  input  in_15,
  input  in_16,
  input  in_17,
  input  in_18,
  input  in_19,
  input  in_20,
  input  in_21,
  input  in_22,
  input  nEN,
  input  \Ф2 ,
  input  nWR,
  input  nRES,
  output MOSI,
  output D7,
  output D6,
  output D5,
  output D4,
  output D3,
  output D2,
  output D1,
  output D0,
  output nBUSY,
  output SCK
);

  wire _74163_1_p5, _74163_1_p12, _74163_1_p13, _74163_1_p14, bussplitter_1_d0, bussplitter_1_d1,
       bussplitter_1_d2, bussplitter_1_d3, bussplitter_1_d4, bussplitter_1_d5, bussplitter_1_d6,
       bussplitter_1_d7, not_1_out, not_2_out, not_3_out, or_1_out, or_2_out;
  wire [7:0] driver_1_out;

  assign driver_1_out = DRIVE ? {in_19, in_21, in_18, in_20, in_17, in_16, in_15, in_22} : 8'bz;  // Driver driver_1
  not not_1 (not_1_out, DRIVE);
  assign {D7, D6, D5, D4, D3, D2, D1, D0} = not_1_out ? driver_1_out : 8'bz;  // Driver driver_2
  or or_1 (or_1_out, nWR, nEN);
  or or_2 (or_2_out, nEN, nRD);
  not not_2 (not_2_out, or_1_out);
  not not_3 (not_3_out, \Ф2 );
  // _74163 _74163_1: pin names not known; wires that end beside it: nRES, or_1_out, not_3_out, 1'b1, _74163_1_p5, 1'b0, 1'b0, 1'b0, 1'b1, 1'b1, 1'b0, _74163_1_p12, _74163_1_p13, _74163_1_p14, nBUSY, _74163_1_p12, _74163_1_p13, _74163_1_p14
  BusSplitter #(.Bits(8)) bussplitter_1 (
    .D(driver_1_out), .OE(DRIVE), .D0(bussplitter_1_d0), .D1(bussplitter_1_d1), .D2(bussplitter_1_d2),
    .D3(bussplitter_1_d3), .D4(bussplitter_1_d4), .D5(bussplitter_1_d5), .D6(bussplitter_1_d6),
    .D7(bussplitter_1_d7));
  not not_4 (_74163_1_p5, nBUSY);
  // _74299 _74299_1: pin names not known; wires that end beside it: MISO, 1'b1, not_2_out, or_2_out, 1'b0, not_3_out, nRES, 1'b0, 1'b1, 1'b0, bussplitter_1_d0, bussplitter_1_d1, bussplitter_1_d2, bussplitter_1_d3, bussplitter_1_d4, bussplitter_1_d5, bussplitter_1_d6, bussplitter_1_d7, MOSI
  and and_1 (SCK, \Ф2 , _74163_1_p5);

  // Notes on the sheet:
  //   MISO: default 1
  //   nRD: default 1
  //   in_16: default 1
  //   in_17: default 1
  //   in_20: default 1
  //   in_22: default 1
  //   nEN: default 1
  //   nWR: default 1
  //   nRES: default 1
  //   MPU
  //   Buffers (for proper simulation)
  //   If ~BUSY is active, new data cannot be written to SPI.
  //   ~BUSY must be memory-mapped somewhere.
  //   If '173 is used for MOSI flip-flop, then one
  //   of its quarters can be used here to tri-state ~BUSY.
  //   Ф2 must go low before ~WR is deactivated to correctly latch data.
  //   On startup, ~RES must be asserted for at least one full Ф2 cycle.
endmodule

/* Test case:
# Reset
~RES DRIVE Ф2 ~EN ~WR ~RD  MISO SCK MOSI ~BUSY D0 D1 D2 D3 D4 D5 D6 D7
1    0     0   1   1   1   0    X   X     X    X  X  X  X  X  X  X  X
0    0     0   1   1   1   0    X   X     X    X  X  X  X  X  X  X  X
0    0     1   1   1   1   0    X   X     X    X  X  X  X  X  X  X  X
0    0     0   1   1   1   0    X   X     X    X  X  X  X  X  X  X  X
1    0     0   1   1   1   0    0   0     X    X  X  X  X  X  X  X  X

# Dummy Ф2 cycle
1    0     0   1   1   1   0    0   0     1    X  X  X  X  X  X  X  X
1    0     1   1   1   1   0    0   0     1    X  X  X  X  X  X  X  X

# SPI device CS should be asserted here.

# Write to buffer
1    0     0   1   1   1   0    0   0     1    X  X  X  X  X  X  X  X
1    1     0   0   0   1   0    0   0     1    X  X  X  X  X  X  X  X
1    1     1   0   0   1   0    0   0     1    X  X  X  X  X  X  X  X
1    1     0   0   0   1   0    0   0     0    X  X  X  X  X  X  X  X
1    0     0   1   1   1   0    0   0     0    X  X  X  X  X  X  X  X

# Send 00011101, receive 11100010

# Transfer bit 7
1    0     1   1   1   1   1    1   0     0    X  X  X  X  X  X  X  X
# Receive bit 7
1    0     0   1   1   1   1    0   0     0    X  X  X  X  X  X  X  X
# Transfer bit 6
1    0     1   1   1   1   1    1   0     0    X  X  X  X  X  X  X  X
# Receive bit 6
1    0     0   1   1   1   1    0   0     0    X  X  X  X  X  X  X  X
# Transfer bit 5
1    0     1   1   1   1   1    1   0     0    X  X  X  X  X  X  X  X
# Receive bit 5
1    0     0   1   1   1   1    0   1     0    X  X  X  X  X  X  X  X
# Transfer bit 4
1    0     1   1   1   1   0    1   1     0    X  X  X  X  X  X  X  X
# Receive bit 4
1    0     0   1   1   1   0    0   1     0    X  X  X  X  X  X  X  X
# Transfer bit 3
1    0     1   1   1   1   0    1   1     0    X  X  X  X  X  X  X  X
# Receive bit 3
1    0     0   1   1   1   0    0   1     0    X  X  X  X  X  X  X  X
# Transfer bit 2
1    0     1   1   1   1   0    1   1     0    X  X  X  X  X  X  X  X
# Receive bit 2
1    0     0   1   1   1   0    0   0     0    X  X  X  X  X  X  X  X
# Transfer bit 1
1    0     1   1   1   1   1    1   0     0    X  X  X  X  X  X  X  X
# Receive bit 1
1    0     0   1   1   1   1    0   1     0    X  X  X  X  X  X  X  X
# Transfer bit 0
1    0     1   1   1   1   0    1   1     0    X  X  X  X  X  X  X  X
# Receive bit 0, back to not busy
1    0     0   1   1   1   0    0   1     1    X  X  X  X  X  X  X  X
# Verify received byte
1    0     0   0   1   0   0    0   1     1    0  1  0  0  0  1  1  1

# SPI device CS should be deasserted here.
*/
