// Digital circuit vpb_v3.dig as structural Verilog
module vpb_v3 (
  input  nIRQ4,
  input  nIRQ3,
  input  nIRQ2,
  input  nIRQ1,
  input  nIRQ0,
  input  D4_2,
  input  D5_2,
  input  D6_2,
  input  D7_2,
  input  ROMnEN,
  input  A0,
  input  nVP,
  input  nIRQ5,
  input  nIRQ6,
  input  nIRQ7,
  output to_CPU_nIRQ,
  output D4,
  output D5,
  output D6,
  output D7
);

  wire _74ls148_1_a0, _74ls148_1_a1, _74ls148_1_a2, or_1_out;

  _74ls148 _74ls148_1 (
    ._0(nIRQ7), ._1(nIRQ6), ._2(nIRQ5), ._3(nIRQ4), ._4(nIRQ3), ._5(nIRQ2), ._6(nIRQ1), ._7(nIRQ0),
    .EI(1'b0), .VCC(1'b1), .GND(1'b0), .GS(to_CPU_nIRQ), .A0(_74ls148_1_a0), .A1(_74ls148_1_a1),
    .A2(_74ls148_1_a2));  // open: EO
  or or_1 (or_1_out, A0, nVP);
  // _74257 _74257_1: pin names not known; wires that end beside it: _74ls148_1_a0, _74ls148_1_a1, _74ls148_1_a2, 1'b0, D4_2, D5_2, D6_2, D7_2, or_1_out, ROMnEN, 1'b1, 1'b0, D4, D5, D6, D7

  // Notes on the sheet:
  //   nIRQ4: default 1
  //   nIRQ3: default 1
  //   nIRQ2: default 1
  //   nIRQ1: default 1
  //   nIRQ0: default 1
  //   nVP: default 1
  //   nIRQ5: default 1
  //   nIRQ6: default 1
  //   nIRQ7: default 1
  //   ~IRQ0 has highest priority
  //   ISR address is partially fetched from ROM.
  //   LSB low nibble set to $FFFE[3..0] (must be zeroed in ROM)
  //   LSB high nibble set to [0,A2,A1,A0]
  //   MSB loaded from ROM @ $FFFF
  //   From
  //   ROM
  //   To CPU
endmodule
